// Logisim project alu.circ as structural Verilog: 1 circuit, main circuit main
module main (
  input  F0,
  input  F2,
  input  F4,
  input  F5,
  input  F6,
  input  MODE,
  input  A,
  input  B,
  input  Cin,
  output R,
  output Cout
);

  wire _0_out, _1_out, _2_out, _3_out, _4_out, _5_out, _6_out, _7_out, _8_out, _9_out, _10_out;

  nand _0 (_0_out, B, F0);
  nand _1 (_1_out, B, _0_out);
  nand _2 (_2_out, _0_out, F2);
  nand _3 (_3_out, _1_out, _2_out);
  nand _5 (_5_out, A, F5, _4_out);
  nand _4 (_4_out, A, F4, _3_out);
  nand _6 (_6_out, _4_out, F6, _3_out);
  nand _7 (_7_out, _5_out, _6_out);
  nand _8 (_8_out, _7_out, MODE, Cin);
  nand _9 (_9_out, _7_out, _8_out);
  nand _11 (R, _9_out, _10_out);
  nand _10 (_10_out, _8_out, MODE, Cin);
  nand _12 (Cout, _8_out, _4_out);
endmodule
