// Logisim project d_ff_6_nand.circ as structural Verilog: 1 circuit, main circuit main
module main (
  input  clk,
  input  d,
  output q,
  output nq
);

  wire nand_1_out, nand_2_out, nand_3_out, nand_4_out;

  nand nand_1 (nand_1_out, nand_4_out, nand_2_out);
  nand nand_2 (nand_2_out, nand_1_out, clk);
  nand nand_3 (nand_3_out, nand_2_out, clk, nand_4_out);
  nand nand_4 (nand_4_out, nand_3_out, d);
  nand nand_5 (q, nand_2_out, nq);
  nand nand_6 (nq, q, nand_3_out);
endmodule
