// Logisim project d_ff_8_nand.circ as structural Verilog: 1 circuit, main circuit main
module main (
  input  d,
  input  p1,
  input  p2,
  output q,
  output nq
);

  wire _1_out, _2_out, _3_out, _4_out, _5_out, _6_out;

  nand _1 (_1_out, d, p1);
  nand _2 (_2_out, _1_out, p1);
  nand _3 (_3_out, _1_out, _4_out);
  nand _4 (_4_out, _3_out, _2_out);
  nand _6 (_6_out, _3_out, p2);
  nand _5 (_5_out, _4_out, p2);
  nand _7 (q, _6_out, nq);
  nand _8 (nq, q, _5_out);
endmodule
