// Logisim project dual_phase.circ as structural Verilog: 2 circuits, main circuit main
module main (
  input  clk,
  output p1,
  output p2
);

  wire d_ff_1_q, d_ff_1_qn, d_ff_2_q, d_ff_2_qn, nand_1_out, nand_2_out, not_1_out, not_2_out, not_3_out;

  not not_1 (not_1_out, not_2_out);
  not not_2 (not_2_out, clk);
  not not_3 (not_3_out, not_1_out);
  D_Flip_Flop d_ff_1 (.clk(not_1_out), .D(d_ff_2_q), .Q(d_ff_1_q), .Qn(d_ff_1_qn));  // open: preset, en, reset
  D_Flip_Flop d_ff_2 (.clk(not_3_out), .D(d_ff_1_qn), .Q(d_ff_2_q), .Qn(d_ff_2_qn));  // open: preset, en, reset
  nand nand_1 (nand_1_out, d_ff_1_q, d_ff_2_q);
  nand nand_2 (nand_2_out, d_ff_1_qn, d_ff_2_qn);
  not not_4 (p1, nand_1_out);
  not not_5 (p2, nand_2_out);
endmodule

module test (
);

  wire clock_1_out, main_1_p1, main_1_p2;

  Clock clock_1 (.out(clock_1_out));
  LED led_1 (.in(clock_1_out));
  LED led_2 (.in(main_1_p1));
  main main_1 (.clk(clock_1_out), .p1(main_1_p1), .p2(main_1_p2));
  LED led_3 (.in(main_1_p2));
endmodule
